# Fritzing sketch attiny85_neopixel (saved by Fritzing 0.9.3b)
breadboards: 1

parts:
  U1 = attiny85 [package=dip]
  S1 = Tilt Switch [package=THT]
  NEOPIXEL1 = Neopixel Strip -- Black (30/m)
  R1 = Resistor [tolerance=±5% resistance=10k package=THT]

nets:
  N1: U1.Pin_3, NEOPIXEL1.Din
  N2: U1.Pin_4, NEOPIXEL1.GND, R1.Pin_1
  N3: U1.Pin_5, S1.Pin_2, R1.Pin_0
  N4: U1.Pin_8, S1.Pin_1, NEOPIXEL1.+5V

custom parts:
  Neopixel Strip -- Black (30/m): These NeoPixel strips have 30 digitally-addressable pixel LEDs per meter and are very affordable and are only 12.5 mm wide, 10 mm if you remove the strip from the casing.
